// Digital circuit 74HC393.dig as structural Verilog
module _74HC393 (
  input  CLK,
  input  CLR,
  output Q_A,
  output Q_B,
  output Q_C,
  output Q_D
);

  wire not_1_out, t_flipflop_async_1_nq, t_flipflop_async_2_nq, t_flipflop_async_3_nq;

  not not_1 (not_1_out, CLK);
  T_flipflop_async t_flipflop_async_1 (
    .SET(1'b0), .T(1'b1), .CLK(not_1_out), .CLR(CLR), .Q(Q_A), .nQ(t_flipflop_async_1_nq));
  T_flipflop_async t_flipflop_async_2 (
    .SET(1'b0), .T(1'b1), .CLK(t_flipflop_async_1_nq), .CLR(CLR), .Q(Q_B), .nQ(t_flipflop_async_2_nq));
  T_flipflop_async t_flipflop_async_3 (
    .SET(1'b0), .T(1'b1), .CLK(t_flipflop_async_2_nq), .CLR(CLR), .Q(Q_C), .nQ(t_flipflop_async_3_nq));
  T_flipflop_async t_flipflop_async_4 (
    .SET(1'b0), .T(1'b1), .CLK(t_flipflop_async_3_nq), .CLR(CLR), .Q(Q_D));  // open: nQ
endmodule
