// Digital circuit BERRExploration.dig as structural Verilog
module BERRExploration (
  input  VCC,
  input  GND,
  input  clk,
  input  in_4,
  output BERR_1,
  output BERR_2,
  output BERR_3
);

  wire _7493_1_pin1, not_1_out;

  PowerSupply powersupply_1 (.VDD(VCC), .GND(GND));
  _74193 _74193_1 (
    .pin1(GND), .pin4(VCC), .pin5(clk), .pin7(BERR_3), .pin8(GND), .pin9(GND), .pin10(GND), .pin11(VCC),
    .pin14(in_4), .pin15(GND), .pin16(VCC));  // open: pin2, pin3, pin6, pin12, pin13
  not not_1 (not_1_out, in_4);
  _7493 _7493_1 (
    .pin1(_7493_1_pin1), .pin2(in_4), .pin3(in_4), .pin5(VCC), .pin10(GND), .pin11(BERR_1),
    .pin12(_7493_1_pin1), .pin14(clk));  // open: pin4, pin6, pin7, pin8, pin9, pin13
  _74163 _74163_1 (
    .pin1(not_1_out), .pin2(clk), .pin3(GND), .pin4(GND), .pin5(GND), .pin6(GND), .pin7(VCC), .pin8(GND),
    .pin9(VCC), .pin10(VCC), .pin11(BERR_2), .pin16(VCC));  // open: pin12, pin13, pin14, pin15

  // Other names for the same wires on the sheet: AS = in_4; E = clk

  // Notes on the sheet:
  //   VCC: default 1
endmodule
