// Digital circuit Bad393.dig as structural Verilog
module Bad393 (
  input  clk,
  output Q_A,
  output Q_B,
  output Q_C,
  output Q_D
);

  wire t_ff_1_nq, t_ff_2_nq, t_ff_3_nq;

  T_FF t_ff_1 (.T(1'b1), .C(clk), .Q(Q_A), .nQ(t_ff_1_nq));
  T_FF t_ff_2 (.T(1'b1), .C(t_ff_1_nq), .Q(Q_B), .nQ(t_ff_2_nq));
  T_FF t_ff_3 (.T(1'b1), .C(t_ff_2_nq), .Q(Q_C), .nQ(t_ff_3_nq));
  T_FF t_ff_4 (.T(1'b1), .C(t_ff_3_nq), .Q(Q_D));  // open: nQ
endmodule
