// Digital circuit ClockSelect.dig as structural Verilog
module ClockSelect (
  input  DIV0,
  input  DIV1,
  input  VCC,
  input  GND,
  input  CLK,
  input  RES,
  output DIV_CLK
);

  wire CLK_2, CLK_4, CLK_8, CLK_16;

  PowerSupply powersupply_1 (.VDD(VCC), .GND(GND));
  _7493 _7493_1 (
    .pin1(CLK_2), .pin2(RES), .pin3(RES), .pin5(VCC), .pin8(CLK_8), .pin9(CLK_4), .pin10(GND),
    .pin11(CLK_16), .pin12(CLK_2), .pin14(CLK));  // open: pin4, pin6, pin7, pin13
  _74153 _74153_1 (
    .pin1(GND), .pin2(DIV1), .pin3(CLK_16), .pin4(CLK_8), .pin5(CLK_4), .pin6(CLK_2), .pin7(DIV_CLK),
    .pin8(GND), .pin10(GND), .pin11(GND), .pin12(GND), .pin13(GND), .pin14(DIV0), .pin15(VCC), .pin16(VCC));  // open: pin9

  // Notes on the sheet:
  //   VCC: pin 8, default 1
  //   GND: pin 4
  //   RES: Active-high reset line, pin 1
endmodule

/* Test case 1/2 clock:
CLK RES  DIV0 DIV1	DIV_CLK
0   1    0    0		0
C   0    0    0		1
C   0    0    0		0
C   0    0    0		1
C   0    0    0		0
C   0    0    0		1
C   0    0    0		0
C   0    0    0		1
C   1    0    0		0
C   0    0    0		1
C   0    0    0		0
C   0    0    0		1
C   0    0    0		0
C   0    0    0		1
C   0    0    0		0
C   0    0    0		1
*/

/* Test case 1/4 clock:
CLK RES  DIV0 DIV1	DIV_CLK
0   1    1    0		0
C   0    1    0		0
C   0    1    0		1
C   0    1    0		1
C   0    1    0		0
C   0    1    0		0
C   0    1    0		1
C   0    1    0		1
C   1    1    0		0
C   0    1    0		0
C   0    1    0		1
C   0    1    0		1
C   0    1    0		0
C   0    1    0		0
C   0    1    0		1
C   0    1    0		1
*/

/* Test case 1/8 clock:
CLK RES  DIV0 DIV1	DIV_CLK
0   1    0    1		0
C   0    0    1		0
C   0    0    1		0
C   0    0    1		0
C   0    0    1		1
C   0    0    1		1
C   0    0    1		1
C   0    0    1		1
C   1    0    1		0
C   0    0    1		0
C   0    0    1		0
C   0    0    1		0
C   0    0    1		1
C   0    0    1		1
C   0    0    1		1
C   0    0    1		1
*/

/* Test case 1/16 clock:
CLK RES  DIV0 DIV1	DIV_CLK
0   1    1    1		0
C   0    1    1		0
C   0    1    1		0
C   0    1    1		0
C   0    1    1		0
C   0    1    1		0
C   0    1    1		0
C   0    1    1		0
C   0    1    1		1
C   0    1    1		1
C   0    1    1		1
C   0    1    1		1
C   0    1    1		1
C   0    1    1		1
C   0    1    1		1
C   0    1    1		1
*/
