// Digital circuit ControlRegister.dig as structural Verilog
module ControlRegister (
  input  D_0,
  input  D_1,
  input  D_2,
  input  D_3,
  input  D_4,
  input  D_5,
  input  D_6,
  input  D_7,
  input  nRES,
  input  nWR,
  input  nRD,
  input  VCC,
  input  GND,
  input  nRN_SET,
  input  nRN_RES,
  input  nITC_SET,
  input  nITC_RES,
  output ITC,
  output UNUSED,
  output IEN,
  output DEN,
  output SEL_1,
  output SEL_0,
  output DIV_1,
  output DIV_0,
  output RUNNING
);

  wire _7474_1_pin13, and_1_out, WR;

  PowerSupply powersupply_1 (.VDD(VCC), .GND(GND));
  and and_1 (and_1_out, nITC_RES, nRES);
  not not_1 (WR, nWR);
  _74273 _74273_1 (
    .pin1(nRES), .pin2(DIV_0), .pin3(D_0), .pin4(D_1), .pin5(DIV_1), .pin6(SEL_0), .pin7(D_2), .pin8(D_3),
    .pin9(SEL_1), .pin10(GND), .pin11(WR), .pin12(DEN), .pin13(D_4), .pin14(D_5), .pin15(IEN),
    .pin16(UNUSED), .pin17(D_6), .pin18(D_7), .pin20(VCC));  // open: pin19
  _7474 _7474_1 (
    .pin1(and_1_out), .pin2(VCC), .pin3(VCC), .pin4(nITC_SET), .pin5(ITC), .pin7(GND), .pin9(RUNNING),
    .pin10(nRN_SET), .pin11(VCC), .pin12(VCC), .pin13(_7474_1_pin13), .pin14(VCC));  // open: pin6, pin8
  _74245 _74245_1 (
    .pin1(VCC), .pin2(DIV_0), .pin3(DIV_1), .pin4(SEL_0), .pin5(SEL_1), .pin6(DEN), .pin7(IEN),
    .pin8(UNUSED), .pin9(ITC), .pin10(GND), .pin11(D_7), .pin12(D_6), .pin13(D_5), .pin14(D_4), .pin15(D_3),
    .pin16(D_2), .pin17(D_1), .pin18(D_0), .pin19(nRD), .pin20(VCC));
  and and_2 (_7474_1_pin13, nRES, nRN_RES);

  // Notes on the sheet:
  //   nRES: default 1
  //   nWR: default 1
  //   nRD: default 1
  //   VCC: pin 26, default 1
  //   GND: pin 13
  //   nRN_SET: default 1
  //   nRN_RES: default 1
  //   nITC_SET: default 1
  //   nITC_RES: default 1
endmodule
