// Digital circuit DTACK.dig as structural Verilog
module DTACK (
  input  nCS_ROM,
  input  nCS_RAM,
  input  nDTACK_MFP,
  input  nDTACK_XPN,
  output nDTACK
);

  wire nand_1_out, nand_2_out, nand_3_out, nand_4_out;

  nand nand_1 (nand_1_out, nCS_ROM, nCS_RAM);
  nand nand_2 (nand_2_out, nDTACK_MFP, nDTACK_XPN);
  nand nand_3 (nand_3_out, nand_1_out, nand_1_out);
  nand nand_4 (nand_4_out, nand_2_out, nand_2_out);
  and and_1 (nDTACK, nand_3_out, nand_4_out);

  // Notes on the sheet:
  //   nDTACK: pin 19
  //   nCS_ROM: pin 2, default 1
  //   nCS_RAM: pin 3, default 1
  //   nDTACK_MFP: pin 9, default 1
  //   nDTACK_XPN: default 1
endmodule
