// Digital circuit DataRegister.dig as structural Verilog
module DataRegister (
  input  CLK,
  input  nRD,
  input  nWR,
  input  D_0,
  input  D_1,
  input  D_2,
  input  D_3,
  input  D_4,
  input  D_5,
  input  D_6,
  input  D_7,
  input  MISO,
  input  TXC,
  output MOSI
);

  wire _74165_1_pin2;

  PullUp pullup_1 (.out(MISO));
  _74595 _74595_1 (
    .pin1(D_1), .pin2(D_2), .pin3(D_3), .pin4(D_4), .pin5(D_5), .pin6(D_6), .pin7(D_7), .pin8(1'b0),
    .pin10(1'b1), .pin11(CLK), .pin12(TXC), .pin13(nRD), .pin14(MISO), .pin15(D_0), .pin16(1'b1));  // open: pin9
  _74165 _74165_1 (
    .pin1(nWR), .pin2(_74165_1_pin2), .pin3(D_4), .pin4(D_5), .pin5(D_6), .pin6(D_7), .pin8(1'b0),
    .pin9(MOSI), .pin10(1'b1), .pin11(D_0), .pin12(D_1), .pin13(D_2), .pin14(D_3), .pin15(1'b0), .pin16(1'b1));  // open: pin7
  not not_1 (_74165_1_pin2, CLK);

  // Notes on the sheet:
  //   MOSI: pin 8
  //   CLK: pin 2
  //   nRD: pin 3, default 1
  //   nWR: pin 4, default 1
  //   D_0: pin 17
  //   D_1: pin 16
  //   D_2: pin 15
  //   D_3: pin 14
  //   D_4: pin 13
  //   D_5: pin 12
  //   D_6: pin 11
  //   D_7: pin 10
  //   MISO: pin 1, default 1
  //   TXC: pin 5
endmodule

/* Test case Transfer:
CLK MISO ~RD ~WR ~RES TXC MOSI D_0 D_1 D_2 D_3 D_4 D_5 D_6 D_7
0   1    1   1   1    1   1    Z   Z   Z   Z   Z   Z   Z   Z
0   1    1   1   0    1   1    Z   Z   Z   Z   Z   Z   Z   Z
0   1    1   1   1    1   1    Z   Z   Z   Z   Z   Z   Z   Z
0   1    1   0   1    0   0    1   0   1   0   1   0   1   0
1   1    1   1   1    0   0    Z   Z   Z   Z   Z   Z   Z   Z
0   0    1   1   1    0   1    Z   Z   Z   Z   Z   Z   Z   Z
1   0    1   1   1    0   1    Z   Z   Z   Z   Z   Z   Z   Z
0   1    1   1   1    0   0    Z   Z   Z   Z   Z   Z   Z   Z
1   1    1   1   1    0   0    Z   Z   Z   Z   Z   Z   Z   Z
*/
