// Digital circuit DeviceSelect.dig as structural Verilog
module DeviceSelect (
  input  VCC,
  input  GND,
  input  SEL_0,
  input  SEL_1,
  input  DEN,
  input  A_0,
  input  RnW,
  input  nCE,
  output nCS_0,
  output nCS_1,
  output nCS_2,
  output nCS_3,
  output nDATA_RD,
  output nDATA_WR,
  output nCTRL_RD,
  output nCTRL_WR
);

  wire not_1_out;

  PowerSupply powersupply_1 (.VDD(VCC), .GND(GND));
  not not_1 (not_1_out, DEN);
  _74139 _74139_1 (
    .pin1(not_1_out), .pin2(SEL_0), .pin3(SEL_1), .pin4(nCS_0), .pin5(nCS_1), .pin6(nCS_2), .pin7(nCS_3),
    .pin8(GND), .pin9(nCTRL_RD), .pin10(nCTRL_WR), .pin11(nDATA_RD), .pin12(nDATA_WR), .pin13(A_0),
    .pin14(RnW), .pin15(nCE), .pin16(VCC));

  // Notes on the sheet:
  //   VCC: pin 16, default 1
  //   GND: pin 8
  //   SEL_0: pin 1
  //   SEL_1: pin 2
  //   DEN: pin 3
  //   nCS_0: pin 4
  //   nCS_1: pin 5
  //   nCS_2: pin 6
  //   nCS_3: pin 7
  //   RnW: default 1
  //   nCE: default 1
endmodule
