// Digital circuit Register_8.dig as structural Verilog
module Register_8 (
  input  WR,
  input  CLK,
  input  [7:0] D_IN,
  input  RD,
  output [7:0] D_OUT
);

  wire [7:0] register_1_q;

  Register register_1 (.D(D_IN[0]), .C(CLK), .en(WR), .Q(register_1_q[0]));
  assign D_OUT = RD ? register_1_q : 8'bz;  // Driver driver_1
  // Pins of 1 and 8 bits meet at D_IN
  // Pins of 1 and 8 bits meet at register_1_q
endmodule
