// Digital circuit ALU.dig as structural Verilog
module ALU (
  input  [15:0] A,
  input  [15:0] B,
  input  [1:0] CTL,
  output [15:0] Y,
  output Z,
  output C,
  output N,
  output V
);

  wire add_1_c_o, xnor_1_out, xor_1_out;
  wire [15:0] add_1_s, and_1_out, multiplexer_1_out, not_1_out, or_1_out;

  assign not_1_out = ~B;  // Not not_1, 16 bits wide
  Multiplexer #(.Bits(16)) multiplexer_1 (.sel(CTL[0]), .in_0(B), .in_1(not_1_out), .out(multiplexer_1_out));
  xnor xnor_1 (xnor_1_out, CTL[0], B[15], A[15]);
  xor xor_1 (xor_1_out, A[15], N);
  assign and_1_out = A & B;  // And and_1, 16 bits wide
  assign or_1_out = A | B;  // Or or_1, 16 bits wide
  Add #(.Bits(16)) add_1 (.a(A), .b(multiplexer_1_out), .c_i(CTL[0]), .s(add_1_s), .c_o(add_1_c_o));
  Multiplexer #(.Selector_Bits(2), .Bits(16)) multiplexer_2 (
    .sel(CTL), .in_0(and_1_out), .in_1(or_1_out), .in_2(add_1_s), .in_3(add_1_s), .out({N, Y[14:0]}));
  and and_2 (C, add_1_c_o, CTL[1]);
  and and_3 (V, CTL[1], xnor_1_out, xor_1_out);
  nor nor_1 (Z, Y[8], Y[9], Y[10], Y[11], Y[12], Y[13], Y[14], N, Y[0], Y[1], Y[2], Y[3], Y[4], Y[5], Y[6], Y[7]);

  assign Y[15] = N;

  // Notes on the sheet:
  //   00: and
  //   01: or
  //   10: add
  //   11: sub
endmodule
