// Digital circuit Buffer16.dig as structural Verilog
module Buffer16 (
  input  nOE,
  input  [15:0] IN,
  output [15:0] OUT
);

  _74245 _74245_1 (
    .pin1(1'b1), .pin2(IN[0]), .pin3(IN[1]), .pin4(IN[2]), .pin5(IN[3]), .pin6(IN[4]), .pin7(IN[5]),
    .pin8(IN[6]), .pin9(IN[7]), .pin10(1'b0), .pin11(OUT[7]), .pin12(OUT[6]), .pin13(OUT[5]), .pin14(OUT[4]),
    .pin15(OUT[3]), .pin16(OUT[2]), .pin17(OUT[1]), .pin18(OUT[0]), .pin19(nOE), .pin20(1'b1));
  _74245 _74245_2 (
    .pin1(1'b1), .pin2(IN[8]), .pin3(IN[9]), .pin4(IN[10]), .pin5(IN[11]), .pin6(IN[12]), .pin7(IN[13]),
    .pin8(IN[14]), .pin9(IN[15]), .pin10(1'b0), .pin11(OUT[15]), .pin12(OUT[14]), .pin13(OUT[13]),
    .pin14(OUT[12]), .pin15(OUT[11]), .pin16(OUT[10]), .pin17(OUT[9]), .pin18(OUT[8]), .pin19(nOE),
    .pin20(1'b1));
endmodule
