// Digital circuit CPU.dig as structural Verilog
module CPU (
  input  [1:0] in_4,
  input  [2:0] in_5,
  input  [2:0] in_6,
  input  [2:0] in_7,
  input  clk,
  input  in_9,
  input  [15:0] in_10,
  output [15:0] out_1,
  output [15:0] out_2,
  output [15:0] out_3
);

  wire dipswitch_1_out;
  wire [15:0] multiplexer_1_out;

  RegisterFile_Bus registerfile_bus_1 (
    .SEL0(in_5), .SEL1(in_6), .WRSEL(in_7), .WRD(multiplexer_1_out), .nWE(in_9), .CLK(clk), .RD0(out_1),
    .RD1(out_2));
  ALU alu_1 (.A(out_1), .B(out_2), .CTL(in_4), .Y(out_3));  // open: Z, C, N, V
  DipSwitch dipswitch_1 (.out(dipswitch_1_out));
  Multiplexer #(.Bits(16)) multiplexer_1 (.sel(dipswitch_1_out), .in_0(in_10), .in_1(out_3), .out(multiplexer_1_out));
endmodule
