// Digital circuit ProgramCounter.dig as structural Verilog
module ProgramCounter (
  input  CLK,
  input  [15:0] PC_IN,
  input  nRES,
  output [15:0] PC_OUT
);

  _74273 _74273_1 (
    .pin1(nRES), .pin2(PC_OUT[0]), .pin3(PC_IN[0]), .pin4(PC_IN[1]), .pin5(PC_OUT[1]), .pin6(PC_OUT[2]),
    .pin7(PC_IN[2]), .pin8(PC_IN[3]), .pin9(PC_OUT[3]), .pin10(1'b0), .pin11(CLK), .pin12(PC_OUT[4]),
    .pin13(PC_IN[4]), .pin14(PC_IN[5]), .pin15(PC_OUT[5]), .pin16(PC_OUT[6]), .pin17(PC_IN[6]),
    .pin18(PC_IN[7]), .pin19(PC_OUT[7]), .pin20(1'b1));
  _74273 _74273_2 (
    .pin1(nRES), .pin2(PC_OUT[8]), .pin3(PC_IN[8]), .pin4(PC_IN[9]), .pin5(PC_OUT[9]), .pin6(PC_OUT[10]),
    .pin7(PC_IN[10]), .pin8(PC_IN[11]), .pin9(PC_OUT[11]), .pin10(1'b0), .pin11(CLK), .pin12(PC_OUT[12]),
    .pin13(PC_IN[12]), .pin14(PC_IN[13]), .pin15(PC_OUT[13]), .pin16(PC_OUT[14]), .pin17(PC_IN[14]),
    .pin18(PC_IN[15]), .pin19(PC_OUT[15]), .pin20(1'b1));

  // Other names for the same wires on the sheet: OUT0 = PC_OUT[0]; OUT1 = PC_OUT[1]; OUT2 = PC_OUT[2];
  //   OUT3 = PC_OUT[3]; OUT4 = PC_OUT[4]; OUT5 = PC_OUT[5]; OUT6 = PC_OUT[6]; OUT7 = PC_OUT[7]; OUT8 = PC_OUT[8];
  //   OUT9 = PC_OUT[9]; OUT10 = PC_OUT[10]; OUT11 = PC_OUT[11]; OUT12 = PC_OUT[12]; OUT13 = PC_OUT[13];
  //   OUT14 = PC_OUT[14]; OUT15 = PC_OUT[15]; IN0 = PC_IN[0]; IN1 = PC_IN[1]; IN2 = PC_IN[2]; IN3 = PC_IN[3];
  //   IN4 = PC_IN[4]; IN5 = PC_IN[5]; IN6 = PC_IN[6]; IN7 = PC_IN[7]; IN8 = PC_IN[8]; IN9 = PC_IN[9];
  //   IN10 = PC_IN[10]; IN11 = PC_IN[11]; IN12 = PC_IN[12]; IN13 = PC_IN[13]; IN14 = PC_IN[14]; IN15 = PC_IN[15]
endmodule
