// Digital circuit Reg16ClrEn.dig as structural Verilog
module Reg16ClrEn (
  input  [15:0] D_IN,
  input  CLK,
  input  nOE,
  output [15:0] D_OUT
);

  Reg8En reg8en_1 (.D_IN(D_IN[7:0]), .CLK(CLK), .nOE(nOE), .D_OUT(D_OUT[7:0]));
  Reg8En reg8en_2 (.D_IN(D_IN[15:8]), .CLK(CLK), .nOE(nOE), .D_OUT(D_OUT[15:8]));
endmodule
