// Digital circuit Reg8En.dig as structural Verilog
module Reg8En (
  input  [7:0] D_IN,
  input  CLK,
  input  nOE,
  output [7:0] D_OUT
);

  _74574 _74574_1 (
    .pin1(nOE), .pin2(D_IN[0]), .pin3(D_IN[1]), .pin4(D_IN[2]), .pin5(D_IN[3]), .pin6(D_IN[4]),
    .pin7(D_IN[5]), .pin8(D_IN[6]), .pin9(D_IN[7]), .pin10(1'b0), .pin11(CLK), .pin12(D_OUT[7]),
    .pin13(D_OUT[6]), .pin14(D_OUT[5]), .pin15(D_OUT[4]), .pin16(D_OUT[3]), .pin17(D_OUT[2]),
    .pin18(D_OUT[1]), .pin19(D_OUT[0]), .pin20(1'b1));
endmodule
