// Digital circuit RegisterFile.dig as structural Verilog
module RegisterFile (
  input  CLK,
  input  [1:0] SEL0,
  input  [1:0] SEL1,
  input  [1:0] WRSEL,
  input  WE,
  input  [15:0] WRD,
  output [15:0] RD0,
  output [15:0] RD1
);

  wire and_1_out, and_2_out, and_3_out, and_4_out, demultiplexer_1_out_0, demultiplexer_1_out_1,
       demultiplexer_1_out_2, demultiplexer_1_out_3;
  wire [15:0] R0_q, R1_q, R2_q, R3_q;

  Demultiplexer #(.Selector_Bits(2)) demultiplexer_1 (
    .sel(WRSEL), .in(1'b1), .out_0(demultiplexer_1_out_0), .out_1(demultiplexer_1_out_1),
    .out_2(demultiplexer_1_out_2), .out_3(demultiplexer_1_out_3));
  and and_1 (and_1_out, WE, demultiplexer_1_out_0);
  and and_2 (and_2_out, WE, demultiplexer_1_out_1);
  and and_3 (and_3_out, WE, demultiplexer_1_out_2);
  and and_4 (and_4_out, WE, demultiplexer_1_out_3);
  Register #(.Bits(16)) R0 (.D(WRD), .C(CLK), .en(and_1_out), .Q(R0_q));
  Register #(.Bits(16)) R1 (.D(WRD), .C(CLK), .en(and_2_out), .Q(R1_q));
  Register #(.Bits(16)) R2 (.D(WRD), .C(CLK), .en(and_3_out), .Q(R2_q));
  Register #(.Bits(16)) R3 (.D(WRD), .C(CLK), .en(and_4_out), .Q(R3_q));
  Multiplexer #(.Selector_Bits(2), .Bits(16)) multiplexer_1 (
    .sel(SEL0), .in_0(R0_q), .in_1(R1_q), .in_2(R2_q), .in_3(R3_q), .out(RD0));
  Multiplexer #(.Selector_Bits(2), .Bits(16)) multiplexer_2 (
    .sel(SEL1), .in_0(R0_q), .in_1(R1_q), .in_2(R2_q), .in_3(R3_q), .out(RD1));
endmodule
