// Digital circuit RegisterFile_Bus.dig as structural Verilog
module RegisterFile_Bus (
  input  [2:0] SEL0,
  input  [2:0] SEL1,
  input  [2:0] WRSEL,
  input  [15:0] WRD,
  input  nWE,
  input  CLK,
  output [15:0] RD0,
  output [15:0] RD1
);

  wire and_1_out, and_2_out, and_3_out, and_4_out, and_5_out, and_6_out, and_7_out, nOE0_RD0, nOE0_RD1,
       nOE1_RD0, nOE1_RD1, nOE2_RD0, nOE2_RD1, nOE3_RD0, nOE3_RD1, nOE4_RD0, nOE4_RD1, nOE5_RD0, nOE5_RD1,
       nOE6_RD0, nOE6_RD1, nOE7_RD0, nOE7_RD1, not_1_out, not_2_out, not_3_out, not_4_out, not_5_out,
       not_6_out, not_7_out, nWE0, nWE1, nWE2, nWE3, nWE4, nWE5, nWE6, nWE7;
  wire [15:0] reg16clren_1_d_out, reg16clren_2_d_out, reg16clren_3_d_out, reg16clren_4_d_out,
       reg16clren_5_d_out, reg16clren_6_d_out, reg16clren_7_d_out;

  _74138 REGSEL0 (
    .pin1(SEL0[0]), .pin2(SEL0[1]), .pin3(SEL0[2]), .pin4(1'b0), .pin5(1'b0), .pin6(1'b1), .pin7(nOE7_RD0),
    .pin8(1'b0), .pin9(nOE6_RD0), .pin10(nOE5_RD0), .pin11(nOE4_RD0), .pin12(nOE3_RD0), .pin13(nOE2_RD0),
    .pin14(nOE1_RD0), .pin15(nOE0_RD0), .pin16(1'b1));
  _74138 REGSEL1 (
    .pin1(SEL1[0]), .pin2(SEL1[1]), .pin3(SEL1[2]), .pin4(1'b0), .pin5(1'b0), .pin6(1'b1), .pin7(nOE7_RD1),
    .pin8(1'b0), .pin9(nOE6_RD1), .pin10(nOE5_RD1), .pin11(nOE4_RD1), .pin12(nOE3_RD1), .pin13(nOE2_RD1),
    .pin14(nOE1_RD1), .pin15(nOE0_RD1), .pin16(1'b1));
  _74138 REGWRSEL (
    .pin1(WRSEL[0]), .pin2(WRSEL[1]), .pin3(WRSEL[2]), .pin4(nWE), .pin5(nWE), .pin6(1'b1), .pin7(nWE7),
    .pin8(1'b0), .pin9(nWE6), .pin10(nWE5), .pin11(nWE4), .pin12(nWE3), .pin13(nWE2), .pin14(nWE1),
    .pin15(nWE0), .pin16(1'b1));
  not not_1 (not_1_out, nWE1);
  not not_2 (not_2_out, nWE2);
  not not_3 (not_3_out, nWE3);
  not not_4 (not_4_out, nWE4);
  not not_5 (not_5_out, nWE5);
  not not_6 (not_6_out, nWE6);
  not not_7 (not_7_out, nWE7);
  and and_1 (and_1_out, CLK, not_1_out);
  and and_2 (and_2_out, CLK, not_2_out);
  and and_3 (and_3_out, CLK, not_3_out);
  and and_4 (and_4_out, CLK, not_4_out);
  and and_5 (and_5_out, CLK, not_5_out);
  and and_6 (and_6_out, CLK, not_6_out);
  and and_7 (and_7_out, CLK, not_7_out);
  Reg16ClrEn reg16clren_1 (.D_IN(WRD), .CLK(and_1_out), .nOE(1'b0), .D_OUT(reg16clren_1_d_out));
  Reg16ClrEn reg16clren_2 (.D_IN(WRD), .CLK(and_2_out), .nOE(1'b0), .D_OUT(reg16clren_2_d_out));
  Reg16ClrEn reg16clren_3 (.D_IN(WRD), .CLK(and_3_out), .nOE(1'b0), .D_OUT(reg16clren_3_d_out));
  Reg16ClrEn reg16clren_4 (.D_IN(WRD), .CLK(and_4_out), .nOE(1'b0), .D_OUT(reg16clren_4_d_out));
  Reg16ClrEn reg16clren_5 (.D_IN(WRD), .CLK(and_5_out), .nOE(1'b0), .D_OUT(reg16clren_5_d_out));
  Reg16ClrEn reg16clren_6 (.D_IN(WRD), .CLK(and_6_out), .nOE(1'b0), .D_OUT(reg16clren_6_d_out));
  Reg16ClrEn reg16clren_7 (.D_IN(WRD), .CLK(and_7_out), .nOE(1'b0), .D_OUT(reg16clren_7_d_out));
  Buffer16 buffer16_1 (.nOE(nOE0_RD0), .IN({16{1'b0}}), .OUT(RD0));
  Buffer16 buffer16_2 (.nOE(nOE0_RD1), .IN({16{1'b0}}), .OUT(RD1));
  Buffer16 buffer16_3 (.nOE(nOE1_RD0), .IN(reg16clren_1_d_out), .OUT(RD0));
  Buffer16 buffer16_4 (.nOE(nOE1_RD1), .IN(reg16clren_1_d_out), .OUT(RD1));
  Buffer16 buffer16_5 (.nOE(nOE2_RD0), .IN(reg16clren_2_d_out), .OUT(RD0));
  Buffer16 buffer16_6 (.nOE(nOE2_RD1), .IN(reg16clren_2_d_out), .OUT(RD1));
  Buffer16 buffer16_7 (.nOE(nOE3_RD0), .IN(reg16clren_3_d_out), .OUT(RD0));
  Buffer16 buffer16_8 (.nOE(nOE3_RD1), .IN(reg16clren_3_d_out), .OUT(RD1));
  Buffer16 buffer16_9 (.nOE(nOE4_RD0), .IN(reg16clren_4_d_out), .OUT(RD0));
  Buffer16 buffer16_10 (.nOE(nOE4_RD1), .IN(reg16clren_4_d_out), .OUT(RD1));
  Buffer16 buffer16_11 (.nOE(nOE5_RD0), .IN(reg16clren_5_d_out), .OUT(RD0));
  Buffer16 buffer16_12 (.nOE(nOE5_RD1), .IN(reg16clren_5_d_out), .OUT(RD1));
  Buffer16 buffer16_13 (.nOE(nOE6_RD0), .IN(reg16clren_6_d_out), .OUT(RD0));
  Buffer16 buffer16_14 (.nOE(nOE6_RD1), .IN(reg16clren_6_d_out), .OUT(RD1));
  Buffer16 buffer16_15 (.nOE(nOE7_RD0), .IN(reg16clren_7_d_out), .OUT(RD0));
  Buffer16 buffer16_16 (.nOE(nOE7_RD1), .IN(reg16clren_7_d_out), .OUT(RD1));
endmodule
