// Digital circuit SPIMaster.dig as structural Verilog
module SPIMaster (
  input  nRES,
  input  MISO,
  input  D_0,
  input  D_1,
  input  D_2,
  input  D_3,
  input  D_4,
  input  D_5,
  input  D_6,
  input  D_7,
  input  nCE,
  input  A_0,
  input  RnW,
  input  VCC,
  input  GND,
  input  clk,
  output MOSI,
  output nCS_0,
  output nCS_1,
  output nCS_2,
  output nCS_3,
  output nIRQ,
  output SPICLK,
  output CLK_2,
  output RUNNING
);

  wire _7474_1_pin13, and_1_out, and_2_out, CLK_4, CLK_8, CLK_16, DEN, DIV_0, DIV_1, DIVCLK, IEN, ITC,
       nand_1_out, nCTRL_RD, nCTRL_WR, nDATA_RD, nDATA_WR, not_1_out, not_2_out, not_3_out, not_4_out,
       not_6_out, nRUNNING, nSAFEDATA_WR, nTXC, SAFECTRL_WR, SEL_0, SEL_1, SEROUT, TXC, UNUSED;

  PowerSupply powersupply_1 (.VDD(VCC), .GND(GND));
  and and_1 (and_1_out, nDATA_WR, nDATA_RD);
  _74273 _74273_1 (
    .pin1(nRES), .pin2(DIV_0), .pin3(D_0), .pin4(D_1), .pin5(DIV_1), .pin6(SEL_0), .pin7(D_2), .pin8(D_3),
    .pin9(SEL_1), .pin10(GND), .pin11(SAFECTRL_WR), .pin12(DEN), .pin13(D_4), .pin14(D_5), .pin15(IEN),
    .pin16(UNUSED), .pin17(D_6), .pin18(D_7), .pin20(VCC));  // open: pin19
  nand nand_1 (nand_1_out, nRES, RUNNING);
  and and_2 (and_2_out, and_1_out, nRES);
  _74HC393 _74hc393_1 ();
  _74HC393 _74hc393_2 ();
  _7474 _7474_1 (
    .pin1(and_2_out), .pin2(VCC), .pin3(VCC), .pin4(nTXC), .pin5(ITC), .pin7(GND), .pin8(nRUNNING),
    .pin9(RUNNING), .pin10(nSAFEDATA_WR), .pin11(VCC), .pin12(VCC), .pin13(_7474_1_pin13), .pin14(VCC));  // open: pin6
  _74245 _74245_1 (
    .pin1(VCC), .pin2(DIV_0), .pin3(DIV_1), .pin4(SEL_0), .pin5(SEL_1), .pin6(DEN), .pin7(IEN),
    .pin8(UNUSED), .pin9(ITC), .pin10(GND), .pin11(D_7), .pin12(D_6), .pin13(D_5), .pin14(D_4), .pin15(D_3),
    .pin16(D_2), .pin17(D_1), .pin18(D_0), .pin19(nCTRL_RD), .pin20(VCC));
  and and_3 (_7474_1_pin13, nRES, nTXC);
  _74HC393 _74hc393_3 ();
  _74595 _74595_1 (
    .pin1(D_1), .pin2(D_2), .pin3(D_3), .pin4(D_4), .pin5(D_5), .pin6(D_6), .pin7(D_7), .pin8(GND),
    .pin10(1'b1), .pin11(SPICLK), .pin12(TXC), .pin13(nDATA_RD), .pin14(MISO), .pin15(D_0), .pin16(VCC));  // open: pin9
  _74153 _74153_1 (
    .pin1(1'b0), .pin2(DIV_1), .pin3(CLK_16), .pin4(CLK_8), .pin5(CLK_4), .pin6(clk), .pin7(DIVCLK),
    .pin8(1'b0), .pin10(1'b0), .pin11(1'b0), .pin12(1'b0), .pin13(1'b0), .pin14(DIV_0), .pin15(1'b1),
    .pin16(1'b1));  // open: pin9
  not not_1 (not_1_out, SEROUT);
  nand nand_2 (MOSI, RUNNING, not_1_out);
  not not_2 (not_2_out, SPICLK);
  _74165 _74165_1 (
    .pin1(nSAFEDATA_WR), .pin2(not_2_out), .pin3(D_4), .pin4(D_5), .pin5(D_6), .pin6(D_7), .pin8(GND),
    .pin9(SEROUT), .pin10(1'b1), .pin11(D_0), .pin12(D_1), .pin13(D_2), .pin14(D_3), .pin15(1'b0), .pin16(VCC));  // open: pin7
  not not_3 (not_3_out, nCTRL_WR);
  nand nand_3 (SAFECTRL_WR, not_3_out, clk);
  nand nand_4 (nSAFEDATA_WR, clk, not_4_out);
  not not_4 (not_4_out, nDATA_WR);
  nand nand_5 (nIRQ, ITC, IEN);
  not not_5 (nTXC, TXC);
  not not_6 (not_6_out, DEN);
  _74139 _74139_1 (
    .pin1(not_6_out), .pin2(SEL_0), .pin3(SEL_1), .pin4(nCS_0), .pin5(nCS_1), .pin6(nCS_2), .pin7(nCS_3),
    .pin8(GND), .pin9(nCTRL_RD), .pin10(nCTRL_WR), .pin11(nDATA_RD), .pin12(nDATA_WR), .pin13(A_0),
    .pin14(RnW), .pin15(nCE), .pin16(VCC));

  assign CLK_2 = clk;

  // Notes on the sheet:
  //   nCE: default 1
  //   nCS_0: pin 4
  //   nCS_1: pin 5
  //   nCS_2: pin 6
  //   nCS_3: pin 7
  //   RnW: default 1
  //   VCC: default 1
  //   FSM
  //   Control Register
  //   CLK Select
  //   Data Register
  //   Control Signals
  //   Device & Register Select
endmodule
