// Digital circuit StateMachine.dig as structural Verilog
module StateMachine (
  input  nRES,
  input  CLK,
  input  VCC,
  input  GND,
  output TXC
);

  wire _7493_1_pin1, nand_1_out, not_1_out;

  PowerSupply powersupply_1 (.VDD(VCC), .GND(GND));
  not not_1 (not_1_out, TXC);
  nand nand_1 (nand_1_out, not_1_out, nRES);
  _7493 _7493_1 (
    .pin1(_7493_1_pin1), .pin2(nand_1_out), .pin3(nand_1_out), .pin5(VCC), .pin10(GND), .pin11(TXC),
    .pin12(_7493_1_pin1), .pin14(CLK));  // open: pin4, pin6, pin7, pin8, pin9, pin13

  // Notes on the sheet:
  //   TXC: pin 5
  //   nRES: pin 2, default 1
  //   CLK: pin 1
  //   VCC: pin 6, default 1
  //   GND: pin 3
endmodule

/* Test case:
CLK ~RES TXC
0   1    0
C   1    0
C   1    0
C   1    0
C   1    0
C   1    0
C   1    0
C   1    0
C   1    0
C   1    0
C   1    0
C   1    0
C   1    0
C   1    0
C   1    1
*/
