// Digital circuit T-flipflop-async.dig as structural Verilog
module T_flipflop_async (
  input  SET,
  input  T,
  input  CLK,
  input  CLR,
  output Q,
  output nQ
);

  wire xor_1_out;

  xor xor_1 (xor_1_out, Q, T);
  D_FF_AS d_ff_as_1 (.Set(SET), .D(xor_1_out), .C(CLK), .Clr(CLR), .Q(Q), .nQ(nQ));
endmodule
