// Digital circuit UniversalDataRegister.dig as structural Verilog
module UniversalDataRegister (
  input  CLK,
  input  nRD,
  input  nWR,
  input  MISO,
  input  RUNNING,
  input  D_0,
  input  D_1,
  input  D_2,
  input  D_3,
  input  D_4,
  input  D_5,
  input  D_6,
  input  D_7,
  input  nRES,
  output MOSI
);

  wire FUNC0, FUNC1, not_1_out;

  PullUp pullup_1 (.out(MISO));
  not not_1 (not_1_out, nWR);
  _74299 _74299_1 (
    .pin1(FUNC0), .pin2(nRD), .pin3(nRD), .pin4(D_6), .pin5(D_4), .pin6(D_2), .pin7(D_0), .pin9(nRES),
    .pin10(1'b0), .pin11(MISO), .pin12(CLK), .pin13(D_1), .pin14(D_3), .pin15(D_5), .pin16(D_7),
    .pin17(MOSI), .pin18(1'b1), .pin19(FUNC1), .pin20(1'b1));  // open: pin8
  or or_1 (FUNC0, not_1_out, RUNNING);
  and and_1 (FUNC1, RUNNING, not_1_out);

  // Notes on the sheet:
  //   CLK: pin 2
  //   nRD: pin 3, default 1
  //   nWR: pin 4, default 1
  //   MISO: pin 1, default 1
  //   RUNNING: pin 5
  //   MOSI: pin 8
  //   D_0: pin 17
  //   D_1: pin 16
  //   D_2: pin 15
  //   D_3: pin 14
  //   D_4: pin 13
  //   D_5: pin 12
  //   D_6: pin 11
  //   D_7: pin 10
  //   nRES: default 1
  //   FUNC	FUNC0	FUNC1
  //   WR	1	1
  //   SHIFT	1	0
  //   IDLE	0	0
endmodule
