// Digital circuit Yamahawk1.dig as structural Verilog
module Yamahawk1 (
  input  in_1,
  input  in_2,
  input  in_3,
  input  in_4
);

  // _74374 _74374_1: pin names not known
  // _7474 _7474_1: pin names not known
endmodule
